// Logisim project ROM_message_spitter.circ as structural Verilog: 1 circuit, main circuit main
module main (
  input  trigger,
  input  reset,
  input  clock,
  output [6:0] out_4
);

  wire or_1_out;
  wire [7:0] counter_1_q;

  or or_1 (or_1_out, trigger, out_4[0], out_4[1], out_4[2], out_4[3], out_4[4], out_4[5], out_4[6]);
  ROM #(.dataWidth(7)) rom_1 (.addr(counter_1_q), .data(out_4));  // open: sel
  Counter counter_1 (.count(or_1_out), .Q(counter_1_q), .clk(clock), .clr(reset));  // open: load, D, carry

  // Notes on the sheet:
  //   start jakwidzi zero to sie zatrzymuje 
  //   contents of rom_1 (hex, n*v repeats v):
  //   0 73 61 6d 70 6c 65 20 74 65 78 74 0 61 62 63 64
endmodule
