// Logisim project SymulatorProfesora.circ as structural Verilog: 5 circuits, main circuit main
module main (
  input  in_1
);

  wire bf, cl_e, cl_s, clk, clk_slow, clock_2_out, clock_3_out, clock_4_out, clock_5_out, main_3_output,
       messages_1_clr, over;
  wire [3:0] main_6_led_score, main_6_led_score_2;
  wire [4:0] main_1_out, slct;
  wire [5:0] gea, gst, main_2_out0, main_2_out6;
  wire [6:0] key, messages_1_msg;
  wire [7:0] main_3_led_lvl, main_6_led_lives, main_6_led_score_3, main_6_led_score_4, main_6_led_score_5,
       main_6_led_students, main_6_led_students_2, main_6_led_students_3;
  wire [15:0] score;
  wire [31:0] eagles_1_led_buffer, main_4_out_4, main_4_out_5, main_4_out_6, main_4_out_7, main_4_out_8,
       main_4_out_9, main_4_out_10, main_4_out_11, main_4_out_12, main_4_out_13, main_4_out_14,
       main_4_out_15, main_4_out_16, main_4_out_17, main_4_out_18, main_4_out_19, main_4_out_20,
       main_4_out_21, main_4_out_22, main_4_out_23, main_4_out_24, main_4_out_25, main_4_out_26,
       main_4_out_27, main_4_out_28, main_4_out_29, main_4_out_30, main_4_out_31, main_4_out_32,
       main_4_out_33, main_4_out_34, main_4_out_35, main_5_led, or_1_out, profesor_1_profesor,
       students_1_led_buffer;

  keyboard_processor_main main_1 (.keyboard(key), .out(main_1_out), .buffer_done(bf));
  Clock clock_1 (.out(clk));
  entity_spawner_main main_2 (
    .clk(clk_slow), .out0(main_2_out0[0]), .out1(main_2_out0[1]), .out2(main_2_out0[2]),
    .out3(main_2_out0[3]), .out4(main_2_out0[4]), .out5(main_2_out0[5]), .out6(main_2_out6[0]),
    .out7(main_2_out6[1]), .out8(main_2_out6[2]), .out9(main_2_out6[3]), .out10(main_2_out6[4]),
    .out11(main_2_out6[5]), .r0(gea[0]), .r1(gea[1]), .r2(gea[2]), .r3(gea[3]), .r4(gea[4]), .r5(gea[5]),
    .r6(gst[0]), .r7(gst[1]), .r8(gst[2]), .r9(gst[3]), .r10(gst[4]), .r11(gst[5]));
  level_handler_main main_3 (
    .\output (main_3_output), .lvl1(clock_3_out), .lvl2(clock_4_out), .lvl3(clock_2_out), .lvl4(clock_5_out),
    .score(score), .reset(in_1), .clk(clk), .led_lvl(main_3_led_lvl));
  Clock #(.highDuration(32), .lowDuration(32)) clock_2 (.out(clock_2_out));
  Clock #(.highDuration(128), .lowDuration(128)) clock_3 (.out(clock_3_out));
  Clock #(.highDuration(64), .lowDuration(64)) clock_4 (.out(clock_4_out));
  Clock #(.highDuration(16), .lowDuration(16)) clock_5 (.out(clock_5_out));
  profesor profesor_1 (.key(main_1_out), .profesor(profesor_1_profesor), .select(slct), .clk(clk));
  messages messages_1 (
    .score(score), .msg(messages_1_msg), .clr(messages_1_clr), .clk(clk));  // open: reset_comp, reset_msgs
  and and_1 (clk_slow, ~over, main_3_output);  // AND_Gate
  eagles eagles_1 (
    .sendA6(main_2_out0[0]), .sendA5(main_2_out0[1]), .sendA4(main_2_out0[2]), .sendA3(main_2_out0[3]),
    .sendA2(main_2_out0[4]), .sendA1(main_2_out0[5]), .professor(profesor_1_profesor), .move(slct),
    .clk__slowed(clk_slow), .led_buffer(eagles_1_led_buffer), .collision(cl_e), .g6(gea[0]), .g5(gea[1]),
    .g4(gea[2]), .g3(gea[3]), .g2(gea[4]), .g1(gea[5]));
  students students_1 (
    .sendA6(main_2_out6[0]), .sendA5(main_2_out6[1]), .sendA4(main_2_out6[2]), .sendA3(main_2_out6[3]),
    .sendA2(main_2_out6[4]), .sendA1(main_2_out6[5]), .professor(profesor_1_profesor), .move(slct),
    .clk__slowed(clk_slow), .led_buffer(students_1_led_buffer), .collision(cl_s), .g6(gst[0]), .g5(gst[1]),
    .g4(gst[2]), .g3(gst[3]), .g2(gst[4]), .g1(gst[5]));
  TTY #(.rows(1), .cols(110)) tty_1 (.data(messages_1_msg), .clk(clk), .clr(messages_1_clr));  // open: we
  _7_Segment_Display u_7_segment_display_1 (
    .g(main_3_led_lvl[1]), .f(main_3_led_lvl[2]), .a(main_3_led_lvl[7]), .b(main_3_led_lvl[6]),
    .e(main_3_led_lvl[3]), .d(main_3_led_lvl[4]), .c(main_3_led_lvl[5]), .dp(main_3_led_lvl[0]));
  DotMatrix #(.matrixcols(32), .matrixrows(32)) dotmatrix_1 (
    .col0(main_4_out_4), .col1(main_4_out_5), .col2(main_4_out_6), .col3(main_4_out_7), .col4(main_4_out_8),
    .col5(main_4_out_9), .col6(main_4_out_10), .col7(main_4_out_11), .col8(main_4_out_12),
    .col9(main_4_out_13), .col10(main_4_out_14), .col11(main_4_out_15), .col12(main_4_out_16),
    .col13(main_4_out_17), .col14(main_4_out_18), .col15(main_4_out_19), .col16(main_4_out_20),
    .col17(main_4_out_21), .col18(main_4_out_22), .col19(main_4_out_23), .col20(main_4_out_24),
    .col21(main_4_out_25), .col22(main_4_out_26), .col23(main_4_out_27), .col24(main_4_out_28),
    .col25(main_4_out_29), .col26(main_4_out_30), .col27(main_4_out_31), .col28(main_4_out_32),
    .col29(main_4_out_33), .col30(main_4_out_34), .col31(main_4_out_35));
  display_buffer_main main_4 (
    .Address(main_5_led), .Select(slct), .out_4(main_4_out_4), .out_5(main_4_out_5), .out_6(main_4_out_6),
    .out_7(main_4_out_7), .out_8(main_4_out_8), .out_9(main_4_out_9), .out_10(main_4_out_10),
    .out_11(main_4_out_11), .out_12(main_4_out_12), .out_13(main_4_out_13), .out_14(main_4_out_14),
    .out_15(main_4_out_15), .out_16(main_4_out_16), .out_17(main_4_out_17), .out_18(main_4_out_18),
    .out_19(main_4_out_19), .out_20(main_4_out_20), .out_21(main_4_out_21), .out_22(main_4_out_22),
    .out_23(main_4_out_23), .out_24(main_4_out_24), .out_25(main_4_out_25), .out_26(main_4_out_26),
    .out_27(main_4_out_27), .out_28(main_4_out_28), .out_29(main_4_out_29), .out_30(main_4_out_30),
    .out_31(main_4_out_31), .out_32(main_4_out_32), .out_33(main_4_out_33), .out_34(main_4_out_34),
    .out_35(main_4_out_35), .Done(bf));
  assign or_1_out = eagles_1_led_buffer | students_1_led_buffer | profesor_1_profesor;  // OR_Gate or_1, 32 bits wide
  game_over_manager_main main_5 (.normal_led(or_1_out), .select(slct), .over(over), .led(main_5_led));
  Keyboard #(.buflen(1)) keyboard_1 (.clk(clk), .re(1'b1), .data(key));  // open: clr, avail
  _7_Segment_Display u_7_segment_display_2 (
    .g(main_6_led_score_5[1]), .f(main_6_led_score_5[2]), .a(main_6_led_score_5[7]),
    .b(main_6_led_score_5[6]), .e(main_6_led_score_5[3]), .d(main_6_led_score_5[4]),
    .c(main_6_led_score_5[5]), .dp(main_6_led_score_5[0]));
  _7_Segment_Display u_7_segment_display_3 (
    .g(main_6_led_score_4[1]), .f(main_6_led_score_4[2]), .a(main_6_led_score_4[7]),
    .b(main_6_led_score_4[6]), .e(main_6_led_score_4[3]), .d(main_6_led_score_4[4]),
    .c(main_6_led_score_4[5]), .dp(main_6_led_score_4[0]));
  score_updater_main main_6 (
    .clk(clk), .led_students({main_6_led_students_3, main_6_led_students_2, main_6_led_students}),
    .led_score({main_6_led_score_5, main_6_led_score_4, main_6_led_score_3, main_6_led_score_2[3:2], main_6_led_score[3:1], main_6_led_score_2[1:0], main_6_led_score[0]}),
    .score(score), .collision__student(cl_s), .collision__eagle(cl_e), .led_lives(main_6_led_lives),
    .its_over(over));
  _7_Segment_Display u_7_segment_display_4 (
    .g(main_6_led_score_3[1]), .f(main_6_led_score_3[2]), .a(main_6_led_score_3[7]),
    .b(main_6_led_score_3[6]), .e(main_6_led_score_3[3]), .d(main_6_led_score_3[4]),
    .c(main_6_led_score_3[5]), .dp(main_6_led_score_3[0]));
  _7_Segment_Display u_7_segment_display_5 (
    .g(main_6_led_students_3[1]), .f(main_6_led_students_3[2]), .a(main_6_led_students_3[7]),
    .b(main_6_led_students_3[6]), .e(main_6_led_students_3[3]), .d(main_6_led_students_3[4]),
    .c(main_6_led_students_3[5]), .dp(main_6_led_students_3[0]));
  _7_Segment_Display u_7_segment_display_6 (
    .g(main_6_led_students_2[1]), .f(main_6_led_students_2[2]), .a(main_6_led_students_2[7]),
    .b(main_6_led_students_2[6]), .e(main_6_led_students_2[3]), .d(main_6_led_students_2[4]),
    .c(main_6_led_students_2[5]), .dp(main_6_led_students_2[0]));
  _7_Segment_Display u_7_segment_display_7 (
    .g(1'b0), .f(1'b1), .a(1'b1), .b(1'b1), .e(1'b1), .d(1'b1), .c(1'b1), .dp(1'b0));
  _7_Segment_Display u_7_segment_display_8 (
    .g(main_6_led_score_2[0]), .f(main_6_led_score_2[1]), .a(main_6_led_score_2[3]),
    .b(main_6_led_score_2[2]), .e(main_6_led_score[1]), .d(main_6_led_score[2]), .c(main_6_led_score[3]),
    .dp(main_6_led_score[0]));
  _7_Segment_Display u_7_segment_display_9 (
    .g(main_6_led_lives[1]), .f(main_6_led_lives[2]), .a(main_6_led_lives[7]), .b(main_6_led_lives[6]),
    .e(main_6_led_lives[3]), .d(main_6_led_lives[4]), .c(main_6_led_lives[5]), .dp(main_6_led_lives[0]));
  _7_Segment_Display u_7_segment_display_10 (
    .g(main_6_led_students[1]), .f(main_6_led_students[2]), .a(main_6_led_students[7]),
    .b(main_6_led_students[6]), .e(main_6_led_students[3]), .d(main_6_led_students[4]),
    .c(main_6_led_students[5]), .dp(main_6_led_students[0]));
  _7_Segment_Display u_7_segment_display_11 (
    .g(1'b0), .f(1'b1), .a(1'b1), .b(1'b1), .e(1'b1), .d(1'b1), .c(1'b1), .dp(1'b0));

  // Notes on the sheet:
  //   Zegar:1 kHz
  //   Prowadzisz zajecia na roku:
  //   keyboard
  //   Sterowanie:
  //   A - w lewo
  //   D - w prawo
  //   PLN
  //   lat do emerytury
  //   zlapanych studentow
  //   Skarbiec Profesora:
endmodule

module students (
  input  sendA6,
  input  sendA5,
  input  sendA4,
  input  sendA3,
  input  sendA2,
  input  sendA1,
  input  [31:0] professor,
  input  [4:0] move,
  input  clk__slowed,
  output g6,
  output g5,
  output g4,
  output g3,
  output [31:0] led_buffer,
  output g2,
  output g1,
  output collision
);

  wire main_1_p4, main_3_p4, main_5_p4, main_7_p4, main_9_p4, main_11_p4;
  wire [31:0] main_1_p6, main_3_p6, main_5_p6, main_7_p6, main_9_p6, main_11_p6, rom_1_data, rom_2_data,
       rom_3_data, rom_4_data, rom_5_data, rom_6_data;

  ROM #(.addrWidth(5), .dataWidth(32)) rom_1 (.addr(move), .data(rom_1_data));  // open: sel
  ROM #(.addrWidth(5), .dataWidth(32)) rom_2 (.addr(move), .data(rom_2_data));  // open: sel
  ROM #(.addrWidth(5), .dataWidth(32)) rom_3 (.addr(move), .data(rom_3_data));  // open: sel
  ROM #(.addrWidth(5), .dataWidth(32)) rom_4 (.addr(move), .data(rom_4_data));  // open: sel
  ROM #(.addrWidth(5), .dataWidth(32)) rom_5 (.addr(move), .data(rom_5_data));  // open: sel
  ROM #(.addrWidth(5), .dataWidth(32)) rom_6 (.addr(move), .data(rom_6_data));  // open: sel
  // student_drop_main main_1: pin names not known; wires that end beside it: rom_1_data, clk__slowed, sendA6, main_1_p4, g6, main_1_p6, g5
  student_catcher_main main_2 (.student(main_1_p6), .catch(main_1_p4), .profesor(professor));
  // student_drop_main main_3: pin names not known; wires that end beside it: rom_2_data, clk__slowed, sendA5, main_3_p4, g5, main_3_p6, g4
  student_catcher_main main_4 (.student(main_3_p6), .catch(main_3_p4), .profesor(professor));
  // student_drop_main main_5: pin names not known; wires that end beside it: rom_3_data, clk__slowed, sendA4, main_5_p4, g4, main_5_p6, g3
  student_catcher_main main_6 (.student(main_5_p6), .catch(main_5_p4), .profesor(professor));
  // student_drop_main main_7: pin names not known; wires that end beside it: rom_4_data, clk__slowed, sendA3, main_7_p4, g3, main_7_p6, g2
  student_catcher_main main_8 (.student(main_7_p6), .catch(main_7_p4), .profesor(professor));
  // student_drop_main main_9: pin names not known; wires that end beside it: rom_5_data, clk__slowed, sendA2, main_9_p4, g2, main_9_p6, g1
  student_catcher_main main_10 (.student(main_9_p6), .catch(main_9_p4), .profesor(professor));
  // student_drop_main main_11: pin names not known; wires that end beside it: rom_6_data, clk__slowed, sendA1, main_11_p4, g1, main_11_p6
  student_catcher_main main_12 (.student(main_11_p6), .catch(main_11_p4), .profesor(professor));
  assign led_buffer = main_1_p6 | main_3_p6 | main_5_p6 | main_7_p6 | main_9_p6 | main_11_p6;  // OR_Gate or_1, 32 bits wide
  or or_2 (collision, main_11_p4, main_9_p4, main_7_p4, main_5_p4, main_3_p4, main_1_p4);

  // Notes on the sheet:
  //   A6
  //   A5
  //   A4
  //   A3
  //   A2
  //   A1
  //   contents of rom_1 (hex, n*v repeats v):
  //   0 50000000 e0000000 50000000
  //   contents of rom_2 (hex, n*v repeats v):
  //   6*0 50000000 e0000000 50000000
  //   contents of rom_3 (hex, n*v repeats v):
  //   12*0 50000000 e0000000 50000000
  //   contents of rom_4 (hex, n*v repeats v):
  //   17*0 50000000 e0000000 50000000
  //   contents of rom_5 (hex, n*v repeats v):
  //   23*0 50000000 e0000000 50000000
  //   contents of rom_6 (hex, n*v repeats v):
  //   28*0 50000000 e0000000 50000000
endmodule

module eagles (
  input  sendA6,
  input  sendA5,
  input  sendA4,
  input  sendA3,
  input  sendA2,
  input  sendA1,
  input  [31:0] professor,
  input  [4:0] move,
  input  clk__slowed,
  output g6,
  output g5,
  output g4,
  output g3,
  output [31:0] led_buffer,
  output g2,
  output g1,
  output collision
);

  wire main_1_p4, main_3_p4, main_5_p4, main_7_p4, main_9_p4, main_11_p4;
  wire [31:0] main_1_p6, main_3_p6, main_5_p6, main_7_p6, main_9_p6, main_11_p6, rom_1_data, rom_2_data,
       rom_3_data, rom_4_data, rom_5_data, rom_6_data;

  ROM #(.addrWidth(5), .dataWidth(32)) rom_1 (.addr(move), .data(rom_1_data));  // open: sel
  ROM #(.addrWidth(5), .dataWidth(32)) rom_2 (.addr(move), .data(rom_2_data));  // open: sel
  ROM #(.addrWidth(5), .dataWidth(32)) rom_3 (.addr(move), .data(rom_3_data));  // open: sel
  ROM #(.addrWidth(5), .dataWidth(32)) rom_4 (.addr(move), .data(rom_4_data));  // open: sel
  ROM #(.addrWidth(5), .dataWidth(32)) rom_5 (.addr(move), .data(rom_5_data));  // open: sel
  ROM #(.addrWidth(5), .dataWidth(32)) rom_6 (.addr(move), .data(rom_6_data));  // open: sel
  // student_drop_main main_1: pin names not known; wires that end beside it: rom_1_data, clk__slowed, sendA6, main_1_p4, g6, main_1_p6, g5
  student_catcher_main main_2 (.student(main_1_p6), .catch(main_1_p4), .profesor(professor));
  // student_drop_main main_3: pin names not known; wires that end beside it: rom_2_data, clk__slowed, sendA5, main_3_p4, g5, main_3_p6, g4
  student_catcher_main main_4 (.student(main_3_p6), .catch(main_3_p4), .profesor(professor));
  // student_drop_main main_5: pin names not known; wires that end beside it: rom_3_data, clk__slowed, sendA4, main_5_p4, g4, main_5_p6, g3
  student_catcher_main main_6 (.student(main_5_p6), .catch(main_5_p4), .profesor(professor));
  // student_drop_main main_7: pin names not known; wires that end beside it: rom_4_data, clk__slowed, sendA3, main_7_p4, g3, main_7_p6, g2
  student_catcher_main main_8 (.student(main_7_p6), .catch(main_7_p4), .profesor(professor));
  // student_drop_main main_9: pin names not known; wires that end beside it: rom_5_data, clk__slowed, sendA2, main_9_p4, g2, main_9_p6, g1
  student_catcher_main main_10 (.student(main_9_p6), .catch(main_9_p4), .profesor(professor));
  // student_drop_main main_11: pin names not known; wires that end beside it: rom_6_data, clk__slowed, sendA1, main_11_p4, g1, main_11_p6
  student_catcher_main main_12 (.student(main_11_p6), .catch(main_11_p4), .profesor(professor));
  assign led_buffer = main_1_p6 | main_3_p6 | main_5_p6 | professor | main_7_p6 | main_9_p6 | main_11_p6;  // OR_Gate or_1, 32 bits wide
  or or_2 (collision, main_11_p4, main_9_p4, main_7_p4, main_5_p4, main_3_p4, main_1_p4);

  // Notes on the sheet:
  //   A6
  //   A5
  //   A4
  //   A3
  //   A2
  //   A1
  //   contents of rom_1 (hex, n*v repeats v):
  //   c0000000 60000000 30000000 60000000 c0000000
  //   contents of rom_2 (hex, n*v repeats v):
  //   5*0 c0000000 60000000 30000000 60000000 c0000000
  //   contents of rom_3 (hex, n*v repeats v):
  //   11*0 c0000000 60000000 30000000 60000000 c0000000
  //   contents of rom_4 (hex, n*v repeats v):
  //   16*0 c0000000 60000000 30000000 60000000 c0000000
  //   contents of rom_5 (hex, n*v repeats v):
  //   22*0 c0000000 60000000 30000000 60000000 c0000000
  //   contents of rom_6 (hex, n*v repeats v):
  //   27*0 c0000000 60000000 30000000 60000000 c0000000
endmodule

module profesor (
  input  [4:0] key,
  input  clk,
  output [31:0] profesor,
  output [4:0] select
);

  wire [4:0] adder_1_out;

  Counter #(.width(5), .max('h1f)) counter_1 (.Q(select), .clk(clk));  // open: load, D, count, carry, clr
  Adder #(.width(5)) adder_1 (.a(key), .b(select), .out(adder_1_out));  // open: cin, cout
  ROM #(.addrWidth(5), .dataWidth(32)) rom_1 (.addr(adder_1_out), .data(profesor));  // open: sel

  // Notes on the sheet:
  //   profesor
  //   contents of rom_1 (hex, n*v repeats v):
  //   27*0 4 7 e 7 4
endmodule

module messages (
  input  [15:0] score,
  input  reset_comp,
  input  reset_msgs,
  input  clk,
  output [6:0] msg,
  output clr
);

  comparator_score_thresholds_main main_1 (.score(score), .reset(reset_comp), .pulse(clr), .clk(clk));  // open: out
  ROM_message_spitter_main main_2 (.clock(clk), .\output (msg), .trigger(clr), .reset(reset_msgs));
endmodule
