// Logisim project level_handler.circ as structural Verilog: 1 circuit, main circuit main
module main (
  input  lvl1,
  input  lvl2,
  input  lvl3,
  input  lvl4,
  input  clk,
  input  [15:0] score,
  input  reset,
  output \output 
);

  wire and_1_out, and_2_out, and_3_out, and_4_out, and_5_out, and_6_out, and_7_out, comparator_1_eq,
       comparator_1_gt, comparator_2_eq, comparator_2_gt, comparator_3_eq, comparator_3_gt, d_ff_1_q,
       d_ff_2_q, d_ff_3_q, demultiplexer_1_out0, demultiplexer_1_out1, demultiplexer_1_out2,
       demultiplexer_1_out3, or_1_out, or_2_out, or_3_out, or_4_out;
  wire [1:0] counter_1_q;

  Comparator #(.width(16), .mode("unsigned")) comparator_1 (
    .a(score), .b(16'ha), .gt(comparator_1_gt), .eq(comparator_1_eq));  // open: lt
  Comparator #(.width(16), .mode("unsigned")) comparator_2 (
    .a(score), .b({16{1'b1}}), .gt(comparator_2_gt), .eq(comparator_2_eq));  // open: lt
  Comparator #(.width(16), .mode("unsigned")) comparator_3 (
    .a(score), .b({16{1'b1}}), .gt(comparator_3_gt), .eq(comparator_3_eq));  // open: lt
  or or_1 (or_1_out, comparator_1_gt, comparator_1_eq);
  or or_2 (or_2_out, comparator_2_gt, comparator_2_eq);
  or or_3 (or_3_out, comparator_3_gt, comparator_3_eq);
  D_Flip_Flop d_ff_1 (.clk(clk), .D(or_1_out), .Q(d_ff_1_q));  // open: Qn, preset, en, reset
  and and_1 (and_1_out, ~d_ff_1_q, or_1_out);  // AND_Gate
  D_Flip_Flop d_ff_2 (.clk(clk), .D(or_2_out), .Q(d_ff_2_q));  // open: Qn, preset, en, reset
  and and_2 (and_2_out, ~d_ff_2_q, or_2_out);  // AND_Gate
  D_Flip_Flop d_ff_3 (.clk(clk), .D(or_3_out), .Q(d_ff_3_q));  // open: Qn, preset, en, reset
  and and_3 (and_3_out, ~d_ff_3_q, or_3_out);  // AND_Gate
  or or_4 (or_4_out, and_1_out, and_2_out, and_3_out);
  Counter #(.width(2), .max('h3)) counter_1 (
    .Q(counter_1_q), .clk(or_4_out), .clr(reset));  // open: load, D, count, carry
  Demultiplexer #(.select(2), .enable("false")) demultiplexer_1 (
    .out0(demultiplexer_1_out0), .out1(demultiplexer_1_out1), .out2(demultiplexer_1_out2),
    .out3(demultiplexer_1_out3), .in(1'b1), .sel(counter_1_q));
  or or_5 (\output , and_5_out, and_4_out, and_7_out, and_6_out);
  and and_4 (and_4_out, demultiplexer_1_out1, lvl2);
  and and_5 (and_5_out, demultiplexer_1_out0, lvl1);
  and and_6 (and_6_out, demultiplexer_1_out3, lvl4);
  and and_7 (and_7_out, demultiplexer_1_out2, lvl3);
endmodule
